# Fritzing sketch ESP8266_3.3FTDI(USB_UART)_SETUP (saved by Fritzing 0.9.3b)
breadboards: 1

parts:
  U1 = ESP8266 WiFi Module [part_number=ESP8266]
  Part1 = FTDI Basic Programmer

nets:
  N1: U1.RXD, Part1.TXO
  N2: U1.VCC, U1.CH_PD, Part1.POWER
  GND: U1.GPIO_0, U1.GND, Part1.GND
  N3: U1.TXD, Part1.RXI

custom parts:
  ESP8266 WiFi Module: Generic WiFi Module based on the ESP8266 with onboard PCB antenna and UART communications
