# Fritzing sketch Light Sensor with LED (saved by Fritzing 0.9.3b)
breadboards: 1

parts:
  R1 = Resistor [tolerance=±5% resistance=270 package=THT]
  Part1 = Arduino Uno (Rev3)
  LED1 = LED - 5mm [color="Red (633nm)" package="5 mm [THT]"]
  U1 = Ambient Light Sensor [package=temt6000-sen]

nets:
  N1: R1.Pin_0, R1.Pin_1, Part1.5V
  N2: Part1.D13/SCK, LED1.anode
  N3: Part1.GND, LED1.cathode, U1.C1

// code stored in the sketch: FritzLightSensorCore.ino
int sensorPin = A0; // select the input pin for the potentiometer
int ledPin = 13; // select the pin for the LED
int sensorValue = 0; // variable to store the value coming from the sensor
 
void setup () 
{
  pinMode (ledPin, OUTPUT);
  Serial.begin (9600);
}
 
void loop () 
{
  sensorValue = analogRead (sensorPin);
  digitalWrite (ledPin, HIGH);
  delay (sensorValue);
  digitalWrite (ledPin, LOW);
  delay (sensorValue);
  Serial.println (sensorValue, DEC);
}
