# Fritzing sketch Touch with rbg lights (saved by Fritzing 0.9.3b)
breadboards: 1

parts:
  R1 = Resistor [tolerance=±20% resistance=220 part_number=i30 package=THT]
  R2 = Resistor [tolerance=±5% resistance=220 package=THT]
  R3 = Resistor [tolerance=±5% resistance=220 package=THT]
  Part1 = Arduino Uno (Rev3)
  LED1 = RGB LED (com. cathode, rgb) [package="5 mm [THT]"]
  U1 = TOUCH [package=touch2]

nets:
  N1: R1.Pin_0, R1.Pin_1, Part1.D7, LED1.red_anode
  N2: R2.Pin_0, R2.Pin_1, Part1.D6_PWM, LED1.green_anode
  N3: R3.Pin_0, R3.Pin_1, Part1.D5_PWM, LED1.blue_anode
  N4: Part1.GND, LED1.common_cathode
  N5: Part1.D2, U1.T2
  N6: Part1.5V, U1.T1

// code stored in the sketch: touchrbg.ino
int in = 2; 
int redPin = 7;
int greenPin = 6;
int bluePin = 5;  

int counter = 0;

int state = HIGH;  
int r;           
int p = LOW;    
long time = 0;       
long debounce = 200;   
void setup()
{
  pinMode(in, INPUT);
  pinMode(redPin, OUTPUT);
  pinMode(greenPin, OUTPUT);
  pinMode(bluePin, OUTPUT);
}
void loop()
{
  r = digitalRead(in);
  if (r == HIGH && p == LOW && millis() - time > debounce) {
    if (counter == 0) {
      counter = 1;
      setColor(170, 0, 255);
    }else if (counter == 1){
      counter = 2;
      setColor(255, 0, 0);
    } else if (counter == 2){
      counter = 3;
      setColor(0, 0, 255);
    } else if (counter == 3) {
      counter = 4;
      setColor(0, 255, 0); 
    } else if (counter == 4) {
      counter = 5;
      setColor(255, 255, 255);
    } else{
      counter = 0;
      state = LOW;
    }
    time = millis();
     
  }
  p = r;
}

void setColor(int redValue, int greenValue, int blueValue) {
  analogWrite(redPin, redValue);
  analogWrite(greenPin, greenValue);
  analogWrite(bluePin, blueValue);
}
