# Fritzing sketch TempSensor (saved by Fritzing 0.9.3b)
breadboards: 2

parts:
  U1 = ESP8266 WiFi Module [part_number=ESP8266]
  Part1 = FTDI Basic Programmer
  YwRobot_Power_Supply1 = YwRobot Breadboard Power Supply [part_number=545043]
  RHT1 = Humidity and Temperature Sensor RHT03

nets:
  N1: U1.RXD, Part1.TXO
  VCC: U1.VCC, U1.GPIO_0, U1.CH_PD, RHT1.Vcc
  N2: U1.GPIO_2, RHT1.Data-signal
  GND: U1.GND, Part1.GND, YwRobot_Power_Supply1.GND#13, RHT1.GND_2
  N3: U1.TXD, Part1.RXI

custom parts:
  ESP8266 WiFi Module: Generic WiFi Module based on the ESP8266 with onboard PCB antenna and UART communications
  YwRobot Breadboard Power Supply: The YwRobot Breadboard Power Supply (MB-V2) has two power rails; they can be 5V or 3V3. Power to the module can be provided through the female USB socket or through the A10 (female) 2.1mm power jack.
