# Fritzing sketch Humidity and Temp with Lights (saved by Fritzing 0.9.3b)
breadboards: 1

parts:
  Part2 = Arduino Uno (Rev3)
  LED2 = RGB LED (com. cathode, rgb) [package="5 mm [THT]"]
  R4 = Resistor [tolerance=±20% resistance=220 part_number=i30 package=THT]
  R5 = Resistor [tolerance=±5% resistance=220 package=THT]
  R6 = Resistor [tolerance=±5% resistance=220 package=THT]
  RHT1 = Humidity and Temperature Sensor RHT03

nets:
  N1: Part2.GND, LED2.common_cathode, RHT1.GND_2
  N2: Part2.D3_PWM, RHT1.Data-signal
  N3: Part2.D5_PWM, LED2.blue_anode, R6.Pin_0, R6.Pin_1
  N4: Part2.D6_PWM, LED2.green_anode, R5.Pin_0, R5.Pin_1
  N5: Part2.D7, LED2.red_anode, R4.Pin_0, R4.Pin_1
  5V: Part2.5V, RHT1.Vcc

// code stored in the sketch: Untitled.ino
/* How to use the DHT-22 sensor with Arduino uno
   Temperature and humidity sensor
   More info: http://www.ardumotive.com/how-to-use-dht-22-sensor-en.html
   Dev: Michalis Vasilakis // Date: 1/7/2015 // www.ardumotive.com */

//Libraries
#include <DHT.h>;

//Constants
#define DHTPIN 2     // what pin we're connected to
#define DHTTYPE DHT22   // DHT 22  (AM2302)
DHT dht(DHTPIN, DHTTYPE); //// Initialize DHT sensor for normal 16mhz Arduino


//Variables
int chk;
float hum;  //Stores humidity value
float temp; //Stores temperature value
int redPin = 7;
int bluePin = 5;
int greenPin = 6;
int counter = 0;

void setup()
{
  Serial.begin(9600);
  dht.begin();
  pinMode(redPin, OUTPUT);
  pinMode(greenPin, OUTPUT);
  pinMode(bluePin, OUTPUT);

}

void loop()
{
  //Read data and store it to variables hum and temp
  hum = dht.readHumidity();
  temp = dht.readTemperature();
  //Print temp and humidity values to serial monitor
  Serial.print("Humidity: ");
  Serial.print(hum);
  Serial.print(" %, Temp: ");
  Serial.print(temp);
  Serial.println(" Celsius");
  if (hum >= 20) {
    switch (counter) {
      case 0:
        setColor(255, 0, 0);
        break;
      case 1:
        setColor(0, 255, 0);
        break;
      case 2:
        setColor(0, 0, 255);
        break;
      case 3:
        setColor(170, 0, 255);
        break;
      case 4:
        setColor(255, 255, 255);
        break;
      default:
        counter = 0;
    }
    counter++;
  }
  else{
      setColor(0,0,0);
  }
    
  
  delay(250);
}

void setColor(int redValue, int greenValue, int blueValue) {
  analogWrite(redPin, redValue);
  analogWrite(greenPin, greenValue);
  analogWrite(bluePin, blueValue);
}
